// Logisim project 2_Logical.circ as structural Verilog: 46 circuits, main circuit main
module main (
  input  in_1,
  input  in_2,
  input  in_3,
  input  in_4,
  input  in_5,
  output out_6,
  output out_7,
  output out_8,
  output out_9
);

  wire decoder_en_4_16_1_out_6, decoder_en_4_16_1_out_7, decoder_en_4_16_1_out_8, decoder_en_4_16_1_out_9,
       decoder_en_4_16_1_out_10, decoder_en_4_16_1_out_11, decoder_en_4_16_1_out_12,
       decoder_en_4_16_1_out_13, decoder_en_4_16_1_out_14, decoder_en_4_16_1_out_15,
       decoder_en_4_16_1_out_16, decoder_en_4_16_1_out_17, decoder_en_4_16_1_out_18,
       decoder_en_4_16_1_out_19, decoder_en_4_16_1_out_20, decoder_en_4_16_1_out_21;

  DECODER_EN_4_16 decoder_en_4_16_1 (
    .in_1(in_1), .in_2(in_2), .in_3(in_3), .in_4(in_4), .EN(in_5), .out_6(decoder_en_4_16_1_out_6),
    .out_7(decoder_en_4_16_1_out_7), .out_8(decoder_en_4_16_1_out_8), .out_9(decoder_en_4_16_1_out_9),
    .out_10(decoder_en_4_16_1_out_10), .out_11(decoder_en_4_16_1_out_11), .out_12(decoder_en_4_16_1_out_12),
    .out_13(decoder_en_4_16_1_out_13), .out_14(decoder_en_4_16_1_out_14), .out_15(decoder_en_4_16_1_out_15),
    .out_16(decoder_en_4_16_1_out_16), .out_17(decoder_en_4_16_1_out_17), .out_18(decoder_en_4_16_1_out_18),
    .out_19(decoder_en_4_16_1_out_19), .out_20(decoder_en_4_16_1_out_20), .out_21(decoder_en_4_16_1_out_21));
  ENCODER_16_4 encoder_16_4_1 (
    .in_1(decoder_en_4_16_1_out_6), .in_2(decoder_en_4_16_1_out_7), .in_3(decoder_en_4_16_1_out_8),
    .in_4(decoder_en_4_16_1_out_9), .in_5(decoder_en_4_16_1_out_10), .in_6(decoder_en_4_16_1_out_11),
    .in_7(decoder_en_4_16_1_out_12), .in_8(decoder_en_4_16_1_out_13), .in_9(decoder_en_4_16_1_out_14),
    .in_10(decoder_en_4_16_1_out_15), .in_11(decoder_en_4_16_1_out_16), .in_12(decoder_en_4_16_1_out_17),
    .in_13(decoder_en_4_16_1_out_18), .in_14(decoder_en_4_16_1_out_19), .in_15(decoder_en_4_16_1_out_20),
    .in_16(decoder_en_4_16_1_out_21), .out_17(out_6), .out_18(out_7), .out_19(out_8), .out_20(out_9));
endmodule

module DECODER_1_2 (
  input  in_1,
  output out_2,
  output out_3
);

  not not_1 (out_2, in_1);

  assign out_3 = in_1;
endmodule

module DECODER2_4 (
  input  in_1,
  input  in_2,
  output out_3,
  output out_4,
  output out_5,
  output out_6
);

  wire not_1_out, not_2_out;

  not not_1 (not_1_out, in_1);
  not not_2 (not_2_out, in_2);
  and and_1 (out_3, not_1_out, not_2_out);
  and and_2 (out_4, in_1, not_2_out);
  and and_3 (out_5, not_1_out, in_2);
  and and_4 (out_6, in_1, in_2);
endmodule

module DECODER3_8 (
  input  in_1,
  input  in_2,
  input  in_3,
  output out_4,
  output out_5,
  output out_6,
  output out_7,
  output out_8,
  output out_9,
  output out_10,
  output out_11
);

  wire decoder2_4_1_out_3, decoder2_4_1_out_4, decoder2_4_1_out_5, decoder2_4_1_out_6, decoder2_4_2_out_3,
       decoder2_4_2_out_4, decoder2_4_2_out_5, decoder2_4_2_out_6, not_1_out;

  not not_1 (not_1_out, in_3);
  DECODER2_4 decoder2_4_1 (
    .in_1(in_1), .in_2(in_2), .out_3(decoder2_4_1_out_3), .out_4(decoder2_4_1_out_4),
    .out_5(decoder2_4_1_out_5), .out_6(decoder2_4_1_out_6));
  DECODER2_4 decoder2_4_2 (
    .in_1(in_1), .in_2(in_2), .out_3(decoder2_4_2_out_3), .out_4(decoder2_4_2_out_4),
    .out_5(decoder2_4_2_out_5), .out_6(decoder2_4_2_out_6));
  and and_1 (out_4, decoder2_4_1_out_3, not_1_out);
  and and_2 (out_5, decoder2_4_1_out_4, not_1_out);
  and and_3 (out_6, decoder2_4_1_out_5, not_1_out);
  and and_4 (out_7, decoder2_4_1_out_6, not_1_out);
  and and_5 (out_8, decoder2_4_2_out_3, in_3);
  and and_6 (out_9, decoder2_4_2_out_4, in_3);
  and and_7 (out_10, decoder2_4_2_out_5, in_3);
  and and_8 (out_11, decoder2_4_2_out_6, in_3);
endmodule

module DECODER_EN_2_4 (
  input  in_1,
  input  in_2,
  input  EN,
  output out_4,
  output out_5,
  output out_6,
  output out_7
);

  wire not_1_out, not_2_out;

  not not_1 (not_1_out, in_1);
  not not_2 (not_2_out, in_2);
  and and_1 (out_4, not_1_out, EN, not_2_out);
  and and_2 (out_5, in_1, EN, not_2_out);
  and and_3 (out_6, not_1_out, EN, in_2);
  and and_4 (out_7, in_1, EN, in_2);
endmodule

module DECODER_EN_3_8 (
  input  in_1,
  input  in_2,
  input  in_3,
  input  EN,
  output out_5,
  output out_6,
  output out_7,
  output out_8,
  output out_9,
  output out_10,
  output out_11,
  output out_12
);

  wire and_1_out, and_2_out, not_1_out;

  not not_1 (not_1_out, in_3);
  and and_1 (and_1_out, not_1_out, EN);
  and and_2 (and_2_out, in_3, EN);
  DECODER_EN_2_4 decoder_en_2_4_1 (
    .in_1(in_1), .in_2(in_2), .EN(and_1_out), .out_4(out_5), .out_5(out_6), .out_6(out_7), .out_7(out_8));
  DECODER_EN_2_4 decoder_en_2_4_2 (
    .in_1(in_1), .in_2(in_2), .EN(and_2_out), .out_4(out_9), .out_5(out_10), .out_6(out_11), .out_7(out_12));
endmodule

module DECODER_EN_4_16 (
  input  in_1,
  input  in_2,
  input  in_3,
  input  in_4,
  input  EN,
  output out_6,
  output out_7,
  output out_8,
  output out_9,
  output out_10,
  output out_11,
  output out_12,
  output out_13,
  output out_14,
  output out_15,
  output out_16,
  output out_17,
  output out_18,
  output out_19,
  output out_20,
  output out_21
);

  wire and_1_out, and_2_out, not_1_out;

  not not_1 (not_1_out, in_4);
  and and_1 (and_1_out, EN, not_1_out);
  and and_2 (and_2_out, in_4, EN);
  DECODER_EN_3_8 decoder_en_3_8_1 (
    .in_1(in_1), .in_2(in_2), .in_3(in_3), .EN(and_1_out), .out_5(out_6), .out_6(out_7), .out_7(out_8),
    .out_8(out_9), .out_9(out_10), .out_10(out_11), .out_11(out_12), .out_12(out_13));
  DECODER_EN_3_8 decoder_en_3_8_2 (
    .in_1(in_1), .in_2(in_2), .in_3(in_3), .EN(and_2_out), .out_5(out_14), .out_6(out_15), .out_7(out_16),
    .out_8(out_17), .out_9(out_18), .out_10(out_19), .out_11(out_20), .out_12(out_21));
endmodule

module SEG_LED (
  input  [15:0] in_1,
  output A,
  output B,
  output C,
  output D,
  output E,
  output F,
  output G
);

  or or_1 (A, in_1[0], in_1[2], in_1[3], in_1[5], in_1[6], in_1[7], in_1[8], in_1[9], in_1[10], in_1[12], in_1[14], in_1[15]);
  or or_2 (B, in_1[0], in_1[1], in_1[2], in_1[3], in_1[4], in_1[7], in_1[8], in_1[9], in_1[10], in_1[13]);
  or or_3 (C, in_1[0], in_1[1], in_1[3], in_1[4], in_1[5], in_1[6], in_1[7], in_1[8], in_1[9], in_1[10], in_1[11], in_1[13]);
  or or_4 (D, in_1[0], in_1[2], in_1[3], in_1[5], in_1[6], in_1[8], in_1[9], in_1[11], in_1[12], in_1[13], in_1[14]);
  or or_5 (E, in_1[0], in_1[2], in_1[6], in_1[8], in_1[10], in_1[11], in_1[12], in_1[13], in_1[14], in_1[15]);
  or or_6 (F, in_1[0], in_1[4], in_1[5], in_1[6], in_1[8], in_1[9], in_1[10], in_1[11], in_1[12], in_1[14], in_1[15]);
  or or_7 (G, in_1[2], in_1[3], in_1[4], in_1[5], in_1[6], in_1[8], in_1[9], in_1[10], in_1[11], in_1[13], in_1[14], in_1[15]);
endmodule

module SEG_LED_DEMO (
  input  in_1,
  input  in_2,
  input  in_3,
  input  in_4,
  input  in_5
);

  wire seg_led_1_a, seg_led_1_b, seg_led_1_c, seg_led_1_d, seg_led_1_e, seg_led_1_f, seg_led_1_g;
  wire [15:0] decoder_en_4_16_1_out_6;

  DECODER_EN_4_16 decoder_en_4_16_1 (
    .in_1(in_1), .in_2(in_2), .in_3(in_3), .in_4(in_4), .EN(in_5), .out_6(decoder_en_4_16_1_out_6[0]),
    .out_7(decoder_en_4_16_1_out_6[1]), .out_8(decoder_en_4_16_1_out_6[2]),
    .out_9(decoder_en_4_16_1_out_6[3]), .out_10(decoder_en_4_16_1_out_6[4]),
    .out_11(decoder_en_4_16_1_out_6[5]), .out_12(decoder_en_4_16_1_out_6[6]),
    .out_13(decoder_en_4_16_1_out_6[7]), .out_14(decoder_en_4_16_1_out_6[8]),
    .out_15(decoder_en_4_16_1_out_6[9]), .out_16(decoder_en_4_16_1_out_6[10]),
    .out_17(decoder_en_4_16_1_out_6[11]), .out_18(decoder_en_4_16_1_out_6[12]),
    .out_19(decoder_en_4_16_1_out_6[13]), .out_20(decoder_en_4_16_1_out_6[14]),
    .out_21(decoder_en_4_16_1_out_6[15]));
  SEG_LED seg_led_1 (
    .in_1(decoder_en_4_16_1_out_6), .A(seg_led_1_a), .B(seg_led_1_b), .C(seg_led_1_c), .D(seg_led_1_d),
    .E(seg_led_1_e), .F(seg_led_1_f), .G(seg_led_1_g));
  _7_Segment_Display u_7_segment_display_1 (
    .g(seg_led_1_g), .f(seg_led_1_f), .a(seg_led_1_a), .b(seg_led_1_b), .e(seg_led_1_e), .d(seg_led_1_d),
    .c(seg_led_1_c));  // open: dp
endmodule

module ENCODER_4_2 (
  input  in_1,
  input  in_2,
  input  in_3,
  input  in_4,
  output out_5,
  output out_6
);

  or or_1 (out_5, in_2, in_4);
  or or_2 (out_6, in_3, in_4);
endmodule

module ENCODER_8_3 (
  input  in_1,
  input  in_2,
  input  in_3,
  input  in_4,
  input  in_5,
  input  in_6,
  input  in_7,
  input  in_8,
  output out_9,
  output out_10,
  output out_11
);

  wire or_1_out, or_2_out, or_3_out, or_4_out;

  or or_1 (or_1_out, in_1, in_5);
  or or_2 (or_2_out, in_2, in_6);
  or or_3 (or_3_out, in_3, in_7);
  or or_4 (or_4_out, in_4, in_8);
  ENCODER_4_2 encoder_4_2_1 (
    .in_1(or_1_out), .in_2(or_2_out), .in_3(or_3_out), .in_4(or_4_out), .out_5(out_9), .out_6(out_10));
  or or_5 (out_11, in_5, in_6, in_7, in_8);
endmodule

module ENCODER_16_4 (
  input  in_1,
  input  in_2,
  input  in_3,
  input  in_4,
  input  in_5,
  input  in_6,
  input  in_7,
  input  in_8,
  input  in_9,
  input  in_10,
  input  in_11,
  input  in_12,
  input  in_13,
  input  in_14,
  input  in_15,
  input  in_16,
  output out_17,
  output out_18,
  output out_19,
  output out_20
);

  wire or_1_out, or_2_out, or_3_out, or_4_out, or_5_out, or_6_out, or_7_out, or_8_out, or_9_out, or_10_out;

  or or_1 (or_1_out, in_1, in_9);
  or or_2 (or_2_out, in_2, in_10);
  or or_3 (or_3_out, in_3, in_11);
  or or_4 (or_4_out, in_4, in_12);
  or or_5 (or_5_out, in_5, in_13);
  or or_6 (or_6_out, in_6, in_14);
  or or_7 (or_7_out, in_7, in_15);
  or or_8 (or_8_out, in_8, in_16);
  or or_9 (or_9_out, in_9, in_10, in_11, in_12);
  or or_10 (or_10_out, in_13, in_14, in_15, in_16);
  or or_11 (out_20, or_9_out, or_10_out);
  ENCODER_8_3 encoder_8_3_1 (
    .in_1(or_1_out), .in_2(or_2_out), .in_3(or_3_out), .in_4(or_4_out), .in_5(or_5_out), .in_6(or_6_out),
    .in_7(or_7_out), .in_8(or_8_out), .out_9(out_17), .out_10(out_18), .out_11(out_19));
endmodule

module PRIORITY_ENCODER_4_2 (
  input  in_1,
  input  in_2,
  input  in_3,
  input  in_4,
  output A0,
  output A1,
  output V
);

  wire and_1_out, not_1_out;

  and and_1 (and_1_out, in_2, not_1_out);
  not not_1 (not_1_out, in_3);
  or or_1 (A0, in_4, and_1_out);
  or or_2 (A1, in_3, in_4);
  or or_3 (V, in_1, in_2, in_3, in_4);
endmodule

module PRIORITY_ENCODER_16_4 (
  input  in_1,
  input  in_2,
  input  in_3,
  input  in_4,
  input  in_5,
  input  in_6,
  input  in_7,
  input  in_8,
  input  in_9,
  input  in_10,
  input  in_11,
  input  in_12,
  input  in_13,
  input  in_14,
  input  in_15,
  input  in_16,
  output [3:0] Y
);

  wire priority_encoder_4_2_1_a0, priority_encoder_4_2_1_a1, priority_encoder_4_2_1_v,
       priority_encoder_4_2_2_a0, priority_encoder_4_2_2_a1, priority_encoder_4_2_2_v,
       priority_encoder_4_2_3_a0, priority_encoder_4_2_3_a1, priority_encoder_4_2_3_v,
       priority_encoder_4_2_4_a0, priority_encoder_4_2_4_a1, priority_encoder_4_2_4_v;

  PRIORITY_ENCODER_4_2 priority_encoder_4_2_1 (
    .in_1(in_1), .in_2(in_2), .in_3(in_3), .in_4(in_4), .A0(priority_encoder_4_2_1_a0),
    .A1(priority_encoder_4_2_1_a1), .V(priority_encoder_4_2_1_v));
  PRIORITY_ENCODER_4_2 priority_encoder_4_2_2 (
    .in_1(in_5), .in_2(in_6), .in_3(in_7), .in_4(in_8), .A0(priority_encoder_4_2_2_a0),
    .A1(priority_encoder_4_2_2_a1), .V(priority_encoder_4_2_2_v));
  PRIORITY_ENCODER_4_2 priority_encoder_4_2_3 (
    .in_1(in_9), .in_2(in_10), .in_3(in_11), .in_4(in_12), .A0(priority_encoder_4_2_3_a0),
    .A1(priority_encoder_4_2_3_a1), .V(priority_encoder_4_2_3_v));
  PRIORITY_ENCODER_4_2 priority_encoder_4_2_4 (
    .in_1(in_13), .in_2(in_14), .in_3(in_15), .in_4(in_16), .A0(priority_encoder_4_2_4_a0),
    .A1(priority_encoder_4_2_4_a1), .V(priority_encoder_4_2_4_v));
  PRIORITY_ENCODER_4_2 priority_encoder_4_2_5 (
    .in_1(priority_encoder_4_2_1_v), .in_2(priority_encoder_4_2_2_v), .in_3(priority_encoder_4_2_3_v),
    .in_4(priority_encoder_4_2_4_v), .A0(Y[2]), .A1(Y[3]));  // open: V
  MUX_1_4_1 mux_1_4_1_1 (
    .I0(priority_encoder_4_2_1_a0), .I1(priority_encoder_4_2_2_a0), .A0(Y[2]), .A1(Y[3]),
    .I2(priority_encoder_4_2_3_a0), .I3(priority_encoder_4_2_4_a0), .Y(Y[0]));
  MUX_1_4_1 mux_1_4_1_2 (
    .I0(priority_encoder_4_2_1_a1), .I1(priority_encoder_4_2_2_a1), .A0(Y[2]), .A1(Y[3]),
    .I2(priority_encoder_4_2_3_a1), .I3(priority_encoder_4_2_4_a1), .Y(Y[1]));
endmodule

module MUX_1_2_1 (
  input  A,
  input  EN,
  input  B,
  output O
);

  wire and_1_out, and_2_out, decoder_1_2_1_out_2, decoder_1_2_1_out_3;

  DECODER_1_2 decoder_1_2_1 (.in_1(EN), .out_2(decoder_1_2_1_out_2), .out_3(decoder_1_2_1_out_3));
  and and_1 (and_1_out, A, decoder_1_2_1_out_2);
  and and_2 (and_2_out, decoder_1_2_1_out_3, B);
  or or_1 (O, and_1_out, and_2_out);
endmodule

module MUX_3_4_1 (
  input  [2:0] I0,
  input  [2:0] I1,
  input  A0,
  input  A1,
  input  [2:0] I2,
  input  [2:0] I3,
  output [2:0] Y
);

  wire decoder2_4_1_out_3, decoder2_4_1_out_4, decoder2_4_1_out_5, decoder2_4_1_out_6;
  wire [2:0] and_1_out, and_4_out, and_7_out, and_10_out;

  DECODER2_4 decoder2_4_1 (
    .in_1(A0), .in_2(A1), .out_3(decoder2_4_1_out_3), .out_4(decoder2_4_1_out_4), .out_5(decoder2_4_1_out_5),
    .out_6(decoder2_4_1_out_6));
  and and_1 (and_1_out[0], I0[0], decoder2_4_1_out_3);
  and and_2 (and_1_out[1], I0[1], decoder2_4_1_out_3);
  and and_3 (and_1_out[2], I0[2], decoder2_4_1_out_3);
  and and_4 (and_4_out[0], I1[0], decoder2_4_1_out_4);
  and and_5 (and_4_out[1], I1[1], decoder2_4_1_out_4);
  and and_6 (and_4_out[2], I1[2], decoder2_4_1_out_4);
  and and_7 (and_7_out[0], I2[0], decoder2_4_1_out_5);
  and and_8 (and_7_out[1], I2[1], decoder2_4_1_out_5);
  and and_9 (and_7_out[2], I2[2], decoder2_4_1_out_5);
  and and_10 (and_10_out[0], I3[0], decoder2_4_1_out_6);
  and and_11 (and_10_out[1], I3[1], decoder2_4_1_out_6);
  and and_12 (and_10_out[2], I3[2], decoder2_4_1_out_6);
  assign Y = and_1_out | and_4_out | and_7_out | and_10_out;  // OR_Gate or_1, 3 bits wide
endmodule

module MUX_3_2_1 (
  input  [2:0] I0,
  input  [2:0] I1,
  input  A0,
  output [2:0] Y
);

  wire decoder_1_2_1_out_2, decoder_1_2_1_out_3;
  wire [2:0] and_1_out, and_4_out;

  DECODER_1_2 decoder_1_2_1 (.in_1(A0), .out_2(decoder_1_2_1_out_2), .out_3(decoder_1_2_1_out_3));
  and and_1 (and_1_out[0], I0[0], decoder_1_2_1_out_2);
  and and_2 (and_1_out[1], I0[1], decoder_1_2_1_out_2);
  and and_3 (and_1_out[2], I0[2], decoder_1_2_1_out_2);
  and and_4 (and_4_out[0], I1[0], decoder_1_2_1_out_3);
  and and_5 (and_4_out[1], I1[1], decoder_1_2_1_out_3);
  and and_6 (and_4_out[2], I1[2], decoder_1_2_1_out_3);
  assign Y = and_1_out | and_4_out;  // OR_Gate or_1, 3 bits wide
endmodule

module MUX_1_4_1 (
  input  I0,
  input  I1,
  input  A0,
  input  A1,
  input  I2,
  input  I3,
  output Y
);

  wire and_1_out, and_2_out, and_3_out, and_4_out, decoder2_4_1_out_3, decoder2_4_1_out_4,
       decoder2_4_1_out_5, decoder2_4_1_out_6;

  DECODER2_4 decoder2_4_1 (
    .in_1(A0), .in_2(A1), .out_3(decoder2_4_1_out_3), .out_4(decoder2_4_1_out_4), .out_5(decoder2_4_1_out_5),
    .out_6(decoder2_4_1_out_6));
  and and_1 (and_1_out, I0, decoder2_4_1_out_3);
  and and_2 (and_2_out, I1, decoder2_4_1_out_4);
  and and_3 (and_3_out, decoder2_4_1_out_5, I2);
  and and_4 (and_4_out, decoder2_4_1_out_6, I3);
  or or_1 (Y, and_1_out, and_2_out, and_3_out, and_4_out);
endmodule

module COMPARE_4 (
  input  [3:0] A0,
  input  [3:0] A1,
  output Y
);

  wire xnor_1_out, xnor_2_out, xnor_3_out, xnor_4_out;

  xnor xnor_1 (xnor_1_out, A0[0], A1[0]);
  xnor xnor_2 (xnor_2_out, A0[1], A1[1]);
  xnor xnor_3 (xnor_3_out, A0[2], A1[2]);
  xnor xnor_4 (xnor_4_out, A0[3], A1[3]);
  and and_1 (Y, xnor_1_out, xnor_2_out, xnor_3_out, xnor_4_out);
  // OR_Gate or_1 is placed but not wired
  // OR_Gate or_2 is placed but not wired
  // OR_Gate or_3 is placed but not wired
endmodule

module COMPARE_DEMO (
);

  wire compare_4_1_y;
  wire [3:0] dipswitch_1_sw1, dipswitch_2_sw1;

  DipSwitch #(.number(4)) dipswitch_1 (
    .sw1(dipswitch_1_sw1[0]), .sw2(dipswitch_1_sw1[1]), .sw3(dipswitch_1_sw1[2]), .sw4(dipswitch_1_sw1[3]));
  DipSwitch #(.number(4)) dipswitch_2 (
    .sw1(dipswitch_2_sw1[0]), .sw2(dipswitch_2_sw1[1]), .sw3(dipswitch_2_sw1[2]), .sw4(dipswitch_2_sw1[3]));
  COMPARE_4 compare_4_1 (.A0(dipswitch_1_sw1), .A1(dipswitch_2_sw1), .Y(compare_4_1_y));
  LED led_1 (.in(compare_4_1_y));
endmodule

module COMPARE_8 (
  input  [7:0] A,
  input  [7:0] B,
  output EQ
);

  wire xnor_1_out, xnor_2_out, xnor_3_out, xnor_4_out, xnor_5_out, xnor_6_out, xnor_7_out, xnor_8_out;

  xnor xnor_1 (xnor_1_out, A[0], B[0]);
  xnor xnor_2 (xnor_2_out, A[1], B[1]);
  xnor xnor_3 (xnor_3_out, A[2], B[2]);
  xnor xnor_4 (xnor_4_out, A[3], B[3]);
  xnor xnor_5 (xnor_5_out, A[4], B[4]);
  xnor xnor_6 (xnor_6_out, A[5], B[5]);
  xnor xnor_7 (xnor_7_out, A[6], B[6]);
  xnor xnor_8 (xnor_8_out, A[7], B[7]);
  and and_1 (EQ, xnor_1_out, xnor_2_out, xnor_3_out, xnor_4_out, xnor_5_out, xnor_6_out, xnor_7_out, xnor_8_out);
endmodule

module FULL_ADDER_1 (
  input  A,
  input  B,
  input  Cin,
  output S,
  output Cout
);

  wire and_1_out, and_2_out, and_3_out, and_4_out, not_1_out, xnor_1_out, xor_1_out;

  xor xor_1 (xor_1_out, A, B);
  and and_1 (and_1_out, A, B);
  xnor xnor_1 (xnor_1_out, A, B);
  not not_1 (not_1_out, Cin);
  and and_2 (and_2_out, xnor_1_out, Cin);
  and and_3 (and_3_out, xor_1_out, not_1_out);
  and and_4 (and_4_out, Cin, xor_1_out);
  or or_1 (S, and_2_out, and_3_out);
  or or_2 (Cout, and_1_out, and_4_out);
endmodule

module HALF_ADDER_1 (
  input  A,
  input  B,
  output S,
  output C
);

  xor xor_1 (S, A, B);
  and and_1 (C, A, B);
endmodule

module FULL_ADDER_HALF (
  input  A,
  input  B,
  input  Cin,
  output S,
  output Cout
);

  wire half_adder_1_1_c, half_adder_1_1_s, half_adder_1_2_c;

  HALF_ADDER_1 half_adder_1_1 (.A(A), .B(B), .S(half_adder_1_1_s), .C(half_adder_1_1_c));
  HALF_ADDER_1 half_adder_1_2 (.A(half_adder_1_1_s), .B(Cin), .S(S), .C(half_adder_1_2_c));
  or or_1 (Cout, half_adder_1_2_c, half_adder_1_1_c);
endmodule

module FULL_ADDER_4 (
  input  A0,
  input  A1,
  input  B0,
  input  B1,
  input  C0,
  input  A2,
  input  A3,
  input  B2,
  input  B3,
  output S1,
  output S0,
  output S3,
  output S2,
  output C3
);

  wire full_adder_1_1_cout, full_adder_1_2_cout, full_adder_1_3_cout;

  FULL_ADDER_1 full_adder_1_1 (.A(A0), .B(B0), .Cin(C0), .S(S0), .Cout(full_adder_1_1_cout));
  FULL_ADDER_1 full_adder_1_2 (.A(A2), .B(B2), .Cin(full_adder_1_3_cout), .S(S2), .Cout(full_adder_1_2_cout));
  FULL_ADDER_1 full_adder_1_3 (.A(A1), .B(B1), .Cin(full_adder_1_1_cout), .S(S1), .Cout(full_adder_1_3_cout));
  FULL_ADDER_1 full_adder_1_4 (.A(A3), .B(B3), .Cin(full_adder_1_2_cout), .S(S3), .Cout(C3));
  LED led_1 (.in(C3));
endmodule

module FULL_ADDER_4_OVERFLOW (
  input  A0,
  input  A1,
  input  B0,
  input  B1,
  input  C0,
  input  A2,
  input  A3,
  input  B2,
  input  B3,
  output S1,
  output S0,
  output S3,
  output S2,
  output C3,
  output Overflow
);

  wire full_adder_1_1_cout, full_adder_1_2_cout, full_adder_1_3_cout;

  FULL_ADDER_1 full_adder_1_1 (.A(A0), .B(B0), .Cin(C0), .S(S0), .Cout(full_adder_1_1_cout));
  FULL_ADDER_1 full_adder_1_2 (.A(A2), .B(B2), .Cin(full_adder_1_3_cout), .S(S2), .Cout(full_adder_1_2_cout));
  xor xor_1 (Overflow, full_adder_1_2_cout, C3);
  FULL_ADDER_1 full_adder_1_3 (.A(A1), .B(B1), .Cin(full_adder_1_1_cout), .S(S1), .Cout(full_adder_1_3_cout));
  FULL_ADDER_1 full_adder_1_4 (.A(A3), .B(B3), .Cin(full_adder_1_2_cout), .S(S3), .Cout(C3));
  LED led_1 (.in(C3));
endmodule

module FULL_ADDER_8_OVERFLOW (
  input  [7:0] A,
  input  [7:0] B,
  input  C0,
  output [7:0] O,
  output C7,
  output Overflow
);

  wire full_adder_1_1_cout, full_adder_1_2_cout, full_adder_1_3_cout, full_adder_1_4_cout,
       full_adder_1_5_cout, full_adder_1_6_cout, full_adder_1_7_cout;

  FULL_ADDER_1 full_adder_1_1 (.A(A[0]), .B(B[0]), .Cin(C0), .S(O[0]), .Cout(full_adder_1_1_cout));
  FULL_ADDER_1 full_adder_1_2 (.A(A[2]), .B(B[2]), .Cin(full_adder_1_5_cout), .S(O[2]), .Cout(full_adder_1_2_cout));
  FULL_ADDER_1 full_adder_1_3 (.A(A[4]), .B(B[4]), .Cin(full_adder_1_6_cout), .S(O[4]), .Cout(full_adder_1_3_cout));
  FULL_ADDER_1 full_adder_1_4 (.A(A[6]), .B(B[6]), .Cin(full_adder_1_7_cout), .S(O[6]), .Cout(full_adder_1_4_cout));
  xor xor_1 (Overflow, full_adder_1_4_cout, C7);
  FULL_ADDER_1 full_adder_1_5 (.A(A[1]), .B(B[1]), .Cin(full_adder_1_1_cout), .S(O[1]), .Cout(full_adder_1_5_cout));
  FULL_ADDER_1 full_adder_1_6 (.A(A[3]), .B(B[3]), .Cin(full_adder_1_2_cout), .S(O[3]), .Cout(full_adder_1_6_cout));
  FULL_ADDER_1 full_adder_1_7 (.A(A[5]), .B(B[5]), .Cin(full_adder_1_3_cout), .S(O[5]), .Cout(full_adder_1_7_cout));
  FULL_ADDER_1 full_adder_1_8 (.A(A[7]), .B(B[7]), .Cin(full_adder_1_4_cout), .S(O[7]), .Cout(C7));
endmodule

module FULL_SUBTRACTOR_1 (
  input  A,
  input  B,
  input  Bin,
  output D,
  output Bout
);

  wire and_1_out, and_2_out, and_3_out, not_1_out, not_2_out, xnor_1_out, xor_1_out;

  xnor xnor_1 (xnor_1_out, B, A);
  xor xor_1 (xor_1_out, A, B);
  and and_1 (and_1_out, xnor_1_out, Bin);
  not not_1 (not_1_out, Bin);
  and and_2 (and_2_out, not_1_out, xor_1_out);
  and and_3 (and_3_out, B, not_2_out);
  not not_2 (not_2_out, A);
  or or_1 (D, and_1_out, and_2_out);
  or or_2 (Bout, and_1_out, and_3_out);
endmodule

module FULL_SUBTRACTOR_4 (
  input  A0,
  input  A1,
  input  B0,
  input  B1,
  input  C0,
  input  A2,
  input  A3,
  input  B2,
  input  B3,
  output D1,
  output D0,
  output D3,
  output D2,
  output Bout3
);

  wire full_subtractor_1_1_bout, full_subtractor_1_2_bout, full_subtractor_1_3_bout;

  FULL_SUBTRACTOR_1 full_subtractor_1_1 (.A(A0), .B(B0), .Bin(C0), .D(D0), .Bout(full_subtractor_1_1_bout));
  FULL_SUBTRACTOR_1 full_subtractor_1_2 (
    .A(A2), .B(B2), .Bin(full_subtractor_1_3_bout), .D(D2), .Bout(full_subtractor_1_2_bout));
  FULL_SUBTRACTOR_1 full_subtractor_1_3 (
    .A(A1), .B(B1), .Bin(full_subtractor_1_1_bout), .D(D1), .Bout(full_subtractor_1_3_bout));
  FULL_SUBTRACTOR_1 full_subtractor_1_4 (.A(A3), .B(B3), .Bin(full_subtractor_1_2_bout), .D(D3), .Bout(Bout3));
  LED led_1 (.in(Bout3));
endmodule

module SAM_ADDER_4 (
  input  [3:0] A,
  input  [3:0] B,
  output [3:0] O
);

  wire abs_val_comparator_4_1_o, mux_1_2_1_1_o, not_1_out, not_2_out, not_3_out, not_4_out, seg_led_1_a,
       seg_led_1_b, seg_led_1_c, seg_led_1_d, seg_led_1_e, seg_led_1_f, seg_led_1_g, xnor_1_out;
  wire [2:0] full_adder_4_1_s0, full_subtractor_4_1_d0, mux_3_2_1_1_y, mux_3_2_1_2_y;
  wire [15:0] decoder_en_4_16_1_out_6;

  ABS_VAL_COMPARATOR_4 abs_val_comparator_4_1 (.A(A), .B(B), .O(abs_val_comparator_4_1_o));
  not not_1 (not_1_out, abs_val_comparator_4_1_o);
  not not_2 (not_2_out, abs_val_comparator_4_1_o);
  xnor xnor_1 (xnor_1_out, A[3], B[3]);
  not not_3 (not_3_out, xnor_1_out);
  MUX_1_2_1 mux_1_2_1_1 (.A(A[3]), .EN(not_2_out), .B(B[3]), .O(mux_1_2_1_1_o));
  MUX_3_2_1 mux_3_2_1_1 (.I0(A[2:0]), .I1(B[2:0]), .A0(not_1_out), .Y(mux_3_2_1_1_y));
  MUX_3_2_1 mux_3_2_1_2 (.I0(A[2:0]), .I1(B[2:0]), .A0(abs_val_comparator_4_1_o), .Y(mux_3_2_1_2_y));
  MUX_1_2_1 mux_1_2_1_2 (.A(A[3]), .EN(not_3_out), .B(mux_1_2_1_1_o), .O(O[3]));
  FULL_ADDER_4 full_adder_4_1 (
    .A0(A[0]), .A1(A[1]), .B0(B[0]), .B1(B[1]), .C0(1'b0), .A2(A[2]), .A3(1'b0), .B2(B[2]), .B3(1'b0),
    .S1(full_adder_4_1_s0[1]), .S0(full_adder_4_1_s0[0]), .S2(full_adder_4_1_s0[2]));  // open: S3, C3
  not not_4 (not_4_out, xnor_1_out);
  FULL_SUBTRACTOR_4 full_subtractor_4_1 (
    .A0(mux_3_2_1_1_y[0]), .A1(mux_3_2_1_1_y[1]), .B0(mux_3_2_1_2_y[0]), .B1(mux_3_2_1_2_y[1]), .C0(1'b0),
    .A2(mux_3_2_1_1_y[2]), .A3(1'b0), .B2(mux_3_2_1_2_y[2]), .B3(1'b0), .D1(full_subtractor_4_1_d0[1]),
    .D0(full_subtractor_4_1_d0[0]), .D2(full_subtractor_4_1_d0[2]));  // open: D3, Bout3
  MUX_3_2_1 mux_3_2_1_3 (.I0(full_adder_4_1_s0), .I1(full_subtractor_4_1_d0), .A0(not_4_out), .Y(O[2:0]));
  DECODER_EN_4_16 decoder_en_4_16_1 (
    .in_1(O[0]), .in_2(O[1]), .in_3(O[2]), .in_4(1'b0), .EN(1'b1), .out_6(decoder_en_4_16_1_out_6[0]),
    .out_7(decoder_en_4_16_1_out_6[1]), .out_8(decoder_en_4_16_1_out_6[2]),
    .out_9(decoder_en_4_16_1_out_6[3]), .out_10(decoder_en_4_16_1_out_6[4]),
    .out_11(decoder_en_4_16_1_out_6[5]), .out_12(decoder_en_4_16_1_out_6[6]),
    .out_13(decoder_en_4_16_1_out_6[7]), .out_14(decoder_en_4_16_1_out_6[8]),
    .out_15(decoder_en_4_16_1_out_6[9]), .out_16(decoder_en_4_16_1_out_6[10]),
    .out_17(decoder_en_4_16_1_out_6[11]), .out_18(decoder_en_4_16_1_out_6[12]),
    .out_19(decoder_en_4_16_1_out_6[13]), .out_20(decoder_en_4_16_1_out_6[14]),
    .out_21(decoder_en_4_16_1_out_6[15]));
  SEG_LED seg_led_1 (
    .in_1(decoder_en_4_16_1_out_6), .A(seg_led_1_a), .B(seg_led_1_b), .C(seg_led_1_c), .D(seg_led_1_d),
    .E(seg_led_1_e), .F(seg_led_1_f), .G(seg_led_1_g));
  _7_Segment_Display u_7_segment_display_1 (.g(O[3]));  // open: f, a, b, e, d, c, dp
  _7_Segment_Display u_7_segment_display_2 (
    .g(seg_led_1_g), .f(seg_led_1_f), .a(seg_led_1_a), .b(seg_led_1_b), .e(seg_led_1_e), .d(seg_led_1_d),
    .c(seg_led_1_c));  // open: dp

  // Notes on the sheet:
  //   4位原码加法器
  //   SAM->Sign And Magnitude
  //   符号相同?1:0
  //   计算绝对值大的数字的符号
  //   供应给符号选择器
  //   分别提供绝对值大的数字与绝对值小的数字
  //   符号选择器
  //   计算加法结果
  //   相同时取其中一个的符号
  //   不同时取绝对值大的符号
  //   计算减法结果（大-小）
  //   结果选择器
  //   符号相同时选取加法结果
  //   符号不同时选取减法结果
  //   组合最终结果
endmodule

module ABS_VAL_COMPARATOR_4 (
  input  [3:0] A,
  input  [3:0] B,
  output O
);

  wire and_1_out, and_2_out, and_3_out, and_4_out, not_1_out, not_2_out, not_3_out, xnor_1_out, xnor_2_out;

  xnor xnor_1 (xnor_1_out, A[2], B[2]);
  not not_1 (not_1_out, B[2]);
  and and_1 (and_1_out, A[2], not_1_out);
  xnor xnor_2 (xnor_2_out, A[1], B[1]);
  not not_2 (not_2_out, B[1]);
  or or_1 (O, and_1_out, and_2_out, and_4_out);
  and and_2 (and_2_out, A[1], xnor_1_out, not_2_out);
  and and_3 (and_3_out, xnor_1_out, xnor_2_out);
  not not_3 (not_3_out, B[0]);
  and and_4 (and_4_out, A[0], and_3_out, not_3_out);

  // Notes on the sheet:
  //   返回 |A|>|B|
  //   本运算用作4位原码加法的绝对值比较器
  //   O=(A2&~B2)|((A2&B2)&A1&~B1)|(((A2&B2)&(A1&B1))&A0&~B0)
endmodule

module SAM_OC_CONVERTER_4 (
  input  [3:0] in_1,
  output [3:0] out_2
);

  wire not_1_out, not_2_out, not_3_out;

  not not_1 (not_1_out, in_1[0]);
  not not_2 (not_2_out, in_1[1]);
  not not_3 (not_3_out, in_1[2]);
  MUX_1_2_1 mux_1_2_1_1 (.A(in_1[0]), .EN(in_1[3]), .B(not_1_out), .O(out_2[0]));
  MUX_1_2_1 mux_1_2_1_2 (.A(in_1[1]), .EN(in_1[3]), .B(not_2_out), .O(out_2[1]));
  MUX_1_2_1 mux_1_2_1_3 (.A(in_1[2]), .EN(in_1[3]), .B(not_3_out), .O(out_2[2]));

  assign out_2[3] = in_1[3];
endmodule

module OC_ADDER_4_V1 (
  input  [3:0] A,
  input  [3:0] B,
  output [3:0] O
);

  wire [3:0] sam_adder_4_1_o, sam_oc_converter_4_1_out_2, sam_oc_converter_4_2_out_2;

  SAM_OC_CONVERTER_4 sam_oc_converter_4_1 (.in_1(A), .out_2(sam_oc_converter_4_1_out_2));
  SAM_OC_CONVERTER_4 sam_oc_converter_4_2 (.in_1(B), .out_2(sam_oc_converter_4_2_out_2));
  SAM_ADDER_4 sam_adder_4_1 (.A(sam_oc_converter_4_1_out_2), .B(sam_oc_converter_4_2_out_2), .O(sam_adder_4_1_o));
  SAM_OC_CONVERTER_4 sam_oc_converter_4_3 (.in_1(sam_adder_4_1_o), .out_2(O));
endmodule

module OC_ADDER_4_V2 (
  input  [3:0] A,
  input  [3:0] B,
  output [3:0] out_3
);

  wire full_adder_4_1_c3, full_adder_4_1_s0, full_adder_4_1_s1, full_adder_4_1_s2, full_adder_4_1_s3;

  FULL_ADDER_4 full_adder_4_1 (
    .A0(A[0]), .A1(A[1]), .B0(B[0]), .B1(B[1]), .C0(1'b0), .A2(A[2]), .A3(A[3]), .B2(B[2]), .B3(B[3]),
    .S1(full_adder_4_1_s1), .S0(full_adder_4_1_s0), .S3(full_adder_4_1_s3), .S2(full_adder_4_1_s2),
    .C3(full_adder_4_1_c3));
  FULL_ADDER_4 full_adder_4_2 (
    .A0(full_adder_4_1_s0), .A1(full_adder_4_1_s1), .B0(1'b0), .B1(1'b0), .C0(full_adder_4_1_c3),
    .A2(full_adder_4_1_s2), .A3(full_adder_4_1_s3), .B2(1'b0), .B3(1'b0), .S1(out_3[1]), .S0(out_3[0]),
    .S3(out_3[3]), .S2(out_3[2]));  // open: C3
endmodule

module TC_ADDER_4 (
  input  [3:0] A,
  input  [3:0] B,
  input  Cin,
  output [3:0] O,
  output Cout,
  output Overflow
);

  FULL_ADDER_4_OVERFLOW full_adder_4_overflow_1 (
    .A0(A[0]), .A1(A[1]), .B0(B[0]), .B1(B[1]), .C0(Cin), .A2(A[2]), .A3(A[3]), .B2(B[2]), .B3(B[3]),
    .S1(O[1]), .S0(O[0]), .S3(O[3]), .S2(O[2]), .C3(Cout), .Overflow(Overflow));
endmodule

module SR_LATCH (
  input  R,
  input  S,
  output Q,
  output NQ
);

  nor nor_1 (Q, R, NQ);
  nor nor_2 (NQ, Q, S);
endmodule

module D_LATCH (
  input  WE,
  input  D,
  output Q,
  output NQ
);

  wire and_1_out, and_2_out, not_1_out;

  not not_1 (not_1_out, D);
  and and_1 (and_1_out, not_1_out, WE);
  and and_2 (and_2_out, WE, D);
  SR_LATCH sr_latch_1 (.R(and_1_out), .S(and_2_out), .Q(Q), .NQ(NQ));
endmodule

module D_LATCH_RST (
  input  RST,
  input  WE,
  input  D,
  output Q,
  output NQ
);

  wire and_1_out, and_2_out, not_1_out, not_2_out, or_1_out;

  not not_1 (not_1_out, RST);
  not not_2 (not_2_out, D);
  and and_1 (and_1_out, not_2_out, WE);
  and and_2 (and_2_out, WE, not_1_out, D);
  or or_1 (or_1_out, RST, and_1_out);
  SR_LATCH sr_latch_1 (.R(or_1_out), .S(and_2_out), .Q(Q), .NQ(NQ));
endmodule

module D_FLIP_FLOP (
  input  CLK,
  input  D,
  output Q
);

  wire d_latch_1_q, not_1_out;

  not not_1 (not_1_out, CLK);
  D_LATCH d_latch_1 (.WE(not_1_out), .D(D), .Q(d_latch_1_q));  // open: NQ
  D_LATCH d_latch_2 (.WE(CLK), .D(d_latch_1_q), .Q(Q));  // open: NQ
endmodule

module D_FLIP_FLOP_RST (
  input  RST,
  input  CLK,
  input  D,
  output Q
);

  wire d_latch_rst_1_q, not_1_out;

  not not_1 (not_1_out, CLK);
  D_LATCH_RST d_latch_rst_1 (.RST(RST), .WE(not_1_out), .D(D), .Q(d_latch_rst_1_q));  // open: NQ
  D_LATCH_RST d_latch_rst_2 (.RST(RST), .WE(CLK), .D(d_latch_rst_1_q), .Q(Q));  // open: NQ
endmodule

module D_FLIP_FLOP_RST_EN (
  input  RST,
  input  EN,
  input  CLK,
  input  D,
  output Q
);

  wire and_1_out, d_latch_rst_1_q, not_1_out;

  and and_1 (and_1_out, EN, CLK);
  not not_1 (not_1_out, and_1_out);
  D_LATCH_RST d_latch_rst_1 (.RST(RST), .WE(not_1_out), .D(D), .Q(d_latch_rst_1_q));  // open: NQ
  D_LATCH_RST d_latch_rst_2 (.RST(RST), .WE(and_1_out), .D(d_latch_rst_1_q), .Q(Q));  // open: NQ
endmodule

module REG_4 (
  input  RST,
  input  EN,
  input  CLK,
  input  D0,
  input  D1,
  input  D2,
  input  D3,
  output Q0,
  output Q1,
  output Q2,
  output Q3
);

  D_FLIP_FLOP_RST_EN d_flip_flop_rst_en_1 (.RST(RST), .EN(EN), .CLK(CLK), .D(D0), .Q(Q0));
  D_FLIP_FLOP_RST_EN d_flip_flop_rst_en_2 (.RST(RST), .EN(EN), .CLK(CLK), .D(D1), .Q(Q1));
  D_FLIP_FLOP_RST_EN d_flip_flop_rst_en_3 (.RST(RST), .EN(EN), .CLK(CLK), .D(D2), .Q(Q2));
  D_FLIP_FLOP_RST_EN d_flip_flop_rst_en_4 (.RST(RST), .EN(EN), .CLK(CLK), .D(D3), .Q(Q3));
endmodule

module REG_8 (
  input  RST,
  input  EN,
  input  CLK,
  input  D0,
  input  D1,
  input  D2,
  input  D3,
  input  D4,
  input  D5,
  input  D6,
  input  D7,
  output Q0,
  output Q1,
  output Q2,
  output Q3,
  output Q4,
  output Q5,
  output Q6,
  output Q7
);

  D_FLIP_FLOP_RST_EN d_flip_flop_rst_en_1 (.RST(RST), .EN(EN), .CLK(CLK), .D(D0), .Q(Q0));
  D_FLIP_FLOP_RST_EN d_flip_flop_rst_en_2 (.RST(RST), .EN(EN), .CLK(CLK), .D(D1), .Q(Q1));
  D_FLIP_FLOP_RST_EN d_flip_flop_rst_en_3 (.RST(RST), .EN(EN), .CLK(CLK), .D(D2), .Q(Q2));
  D_FLIP_FLOP_RST_EN d_flip_flop_rst_en_4 (.RST(RST), .EN(EN), .CLK(CLK), .D(D3), .Q(Q3));
  D_FLIP_FLOP_RST_EN d_flip_flop_rst_en_5 (.RST(RST), .EN(EN), .CLK(CLK), .D(D4), .Q(Q4));
  D_FLIP_FLOP_RST_EN d_flip_flop_rst_en_6 (.RST(RST), .EN(EN), .CLK(CLK), .D(D5), .Q(Q5));
  D_FLIP_FLOP_RST_EN d_flip_flop_rst_en_7 (.RST(RST), .EN(EN), .CLK(CLK), .D(D6), .Q(Q6));
  D_FLIP_FLOP_RST_EN d_flip_flop_rst_en_8 (.RST(RST), .EN(EN), .CLK(CLK), .D(D7), .Q(Q7));
endmodule

module DEMO_SELF_ADDER_4 (
  input  in_1,
  input  in_2,
  output [3:0] out_3
);

  wire clock_1_out;
  wire [3:0] reg_4_1_q0;

  Clock clock_1 (.out(clock_1_out));
  REG_4 reg_4_1 (
    .RST(in_1), .EN(in_2), .CLK(clock_1_out), .D0(out_3[0]), .D1(out_3[1]), .D2(out_3[2]), .D3(out_3[3]),
    .Q0(reg_4_1_q0[0]), .Q1(reg_4_1_q0[1]), .Q2(reg_4_1_q0[2]), .Q3(reg_4_1_q0[3]));
  TC_ADDER_4 tc_adder_4_1 (.A(reg_4_1_q0), .B(4'b0001), .O(out_3));  // open: Cin, Cout, Overflow
endmodule

module DEMO_SEQ_SUM (
  input  RST,
  output [7:0] out_2,
  output [7:0] out_3
);

  wire CLK_out, compare_8_1_eq, not_1_out, xor_1_out;
  wire [7:0] full_adder_8_overflow_2_o, reg_8_1_q0;

  Clock CLK (.out(CLK_out));
  xor xor_1 (xor_1_out, compare_8_1_eq, 1'b1);
  REG_8 reg_8_1 (
    .RST(RST), .EN(not_1_out), .CLK(CLK_out), .D0(out_3[0]), .D1(out_3[1]), .D2(out_3[2]), .D3(out_3[3]),
    .D4(out_3[4]), .D5(out_3[5]), .D6(out_3[6]), .D7(out_3[7]), .Q0(reg_8_1_q0[0]), .Q1(reg_8_1_q0[1]),
    .Q2(reg_8_1_q0[2]), .Q3(reg_8_1_q0[3]), .Q4(reg_8_1_q0[4]), .Q5(reg_8_1_q0[5]), .Q6(reg_8_1_q0[6]),
    .Q7(reg_8_1_q0[7]));
  COMPARE_8 compare_8_1 (.A(reg_8_1_q0), .B(8'hb), .EQ(compare_8_1_eq));
  FULL_ADDER_8_OVERFLOW full_adder_8_overflow_1 (
    .A(reg_8_1_q0), .B({8{1'b0}}), .C0(xor_1_out), .O(out_3));  // open: C7, Overflow
  not not_1 (not_1_out, compare_8_1_eq);
  REG_8 reg_8_2 (
    .RST(RST), .EN(not_1_out), .CLK(CLK_out), .D0(full_adder_8_overflow_2_o[0]),
    .D1(full_adder_8_overflow_2_o[1]), .D2(full_adder_8_overflow_2_o[2]), .D3(full_adder_8_overflow_2_o[3]),
    .D4(full_adder_8_overflow_2_o[4]), .D5(full_adder_8_overflow_2_o[5]), .D6(full_adder_8_overflow_2_o[6]),
    .D7(full_adder_8_overflow_2_o[7]), .Q0(out_2[0]), .Q1(out_2[1]), .Q2(out_2[2]), .Q3(out_2[3]),
    .Q4(out_2[4]), .Q5(out_2[5]), .Q6(out_2[6]), .Q7(out_2[7]));
  FULL_ADDER_8_OVERFLOW full_adder_8_overflow_2 (
    .A(out_2), .B(reg_8_1_q0), .O(full_adder_8_overflow_2_o));  // open: C0, C7, Overflow

  // Notes on the sheet:
  //   EN
endmodule

module DEMO_DIGITAL_CLOCK (
  input  in_1,
  input  in_2
);

  wire and_1_out, and_2_out, binary_to_bcd_converter_3_p2, clock_1_out, compare_4_1_y, compare_4_2_y,
       compare_4_3_y, compare_4_4_y, compare_4_5_y, compare_4_6_y, compare_4_7_y, n7_segment_display_1_p1,
       n7_segment_display_1_p2, n7_segment_display_3_p2, or_1_out, or_2_out, or_3_out, or_4_out;
  wire [3:0] binary_to_bcd_converter_2_p1, binary_to_bcd_converter_3_p1, binary_to_bcd_converter_4_p1,
       reg_4_1_q0, tc_adder_4_1_o, tc_adder_4_2_o, tc_adder_4_3_o, tc_adder_4_4_o;

  Clock clock_1 (.out(clock_1_out));
  or or_1 (or_1_out, in_1, compare_4_1_y);
  REG_4 reg_4_1 (
    .RST(or_1_out), .EN(in_2), .CLK(clock_1_out), .D0(tc_adder_4_1_o[0]), .D1(tc_adder_4_1_o[1]),
    .D2(tc_adder_4_1_o[2]), .D3(tc_adder_4_1_o[3]), .Q0(reg_4_1_q0[0]), .Q1(reg_4_1_q0[1]),
    .Q2(reg_4_1_q0[2]), .Q3(reg_4_1_q0[3]));
  COMPARE_4 compare_4_1 (.A0(reg_4_1_q0), .A1(4'b1111), .Y(compare_4_1_y));
  TC_ADDER_4 tc_adder_4_1 (.A(reg_4_1_q0), .Cin(and_1_out), .O(tc_adder_4_1_o));  // open: B, Cout, Overflow
  // _7_Segment_Display 7_segment_display_1: pin names not known; wires that end beside it: n7_segment_display_1_p1, n7_segment_display_1_p2
  _7_Segment_Display u_7_segment_display_2 ();  // open: g, f, a, b, e, d, c, dp
  // BCD_to_7_Segment_decoder bcd_to_7_segment_decoder_1: pin names not known
  // BCD_to_7_Segment_decoder bcd_to_7_segment_decoder_2: pin names not known
  // Binary_to_BCD_converter #(.binvalue(4)) binary_to_bcd_converter_1: pin names not known; wires that end beside it: reg_4_1_q0, n7_segment_display_1_p1
  // Binary_to_BCD_converter #(.binvalue(4)) binary_to_bcd_converter_2: pin names not known; wires that end beside it: binary_to_bcd_converter_2_p1, n7_segment_display_1_p2
  and and_1 (and_1_out, compare_4_3_y, and_2_out);
  or or_2 (or_2_out, in_1, compare_4_2_y);
  REG_4 reg_4_2 (
    .RST(or_2_out), .EN(in_2), .CLK(clock_1_out), .D0(tc_adder_4_2_o[0]), .D1(tc_adder_4_2_o[1]),
    .D2(tc_adder_4_2_o[2]), .D3(tc_adder_4_2_o[3]), .Q0(binary_to_bcd_converter_2_p1[0]),
    .Q1(binary_to_bcd_converter_2_p1[1]), .Q2(binary_to_bcd_converter_2_p1[2]),
    .Q3(binary_to_bcd_converter_2_p1[3]));
  COMPARE_4 compare_4_2 (.A0(binary_to_bcd_converter_2_p1), .A1(4'b1010), .Y(compare_4_2_y));
  TC_ADDER_4 tc_adder_4_2 (
    .A(binary_to_bcd_converter_2_p1), .Cin(and_2_out), .O(tc_adder_4_2_o));  // open: B, Cout, Overflow
  COMPARE_4 compare_4_3 (.A0(binary_to_bcd_converter_2_p1), .A1(4'b1001), .Y(compare_4_3_y));
  and and_2 (and_2_out, compare_4_7_y, compare_4_5_y);
  or or_3 (or_3_out, in_1, compare_4_4_y);
  // Binary_to_BCD_converter #(.binvalue(4)) binary_to_bcd_converter_3: pin names not known; wires that end beside it: binary_to_bcd_converter_3_p1, binary_to_bcd_converter_3_p2
  REG_4 reg_4_3 (
    .RST(or_3_out), .EN(in_2), .CLK(clock_1_out), .D0(tc_adder_4_3_o[0]), .D1(tc_adder_4_3_o[1]),
    .D2(tc_adder_4_3_o[2]), .D3(tc_adder_4_3_o[3]), .Q0(binary_to_bcd_converter_3_p1[0]),
    .Q1(binary_to_bcd_converter_3_p1[1]), .Q2(binary_to_bcd_converter_3_p1[2]),
    .Q3(binary_to_bcd_converter_3_p1[3]));
  COMPARE_4 compare_4_4 (.A0(binary_to_bcd_converter_3_p1), .A1(4'b0110), .Y(compare_4_4_y));
  TC_ADDER_4 tc_adder_4_3 (
    .A(binary_to_bcd_converter_3_p1), .Cin(compare_4_7_y), .O(tc_adder_4_3_o));  // open: B, Cout, Overflow
  COMPARE_4 compare_4_5 (.A0(binary_to_bcd_converter_3_p1), .A1(4'b0101), .Y(compare_4_5_y));
  // _7_Segment_Display 7_segment_display_3: pin names not known; wires that end beside it: binary_to_bcd_converter_3_p2, n7_segment_display_3_p2
  _7_Segment_Display u_7_segment_display_4 ();  // open: g, f, a, b, e, d, c, dp
  // BCD_to_7_Segment_decoder bcd_to_7_segment_decoder_3: pin names not known
  // BCD_to_7_Segment_decoder bcd_to_7_segment_decoder_4: pin names not known
  // Binary_to_BCD_converter #(.binvalue(4)) binary_to_bcd_converter_4: pin names not known; wires that end beside it: binary_to_bcd_converter_4_p1, n7_segment_display_3_p2
  or or_4 (or_4_out, in_1, compare_4_6_y);
  REG_4 reg_4_4 (
    .RST(or_4_out), .EN(in_2), .CLK(clock_1_out), .D0(tc_adder_4_4_o[0]), .D1(tc_adder_4_4_o[1]),
    .D2(tc_adder_4_4_o[2]), .D3(tc_adder_4_4_o[3]), .Q0(binary_to_bcd_converter_4_p1[0]),
    .Q1(binary_to_bcd_converter_4_p1[1]), .Q2(binary_to_bcd_converter_4_p1[2]),
    .Q3(binary_to_bcd_converter_4_p1[3]));
  COMPARE_4 compare_4_6 (.A0(binary_to_bcd_converter_4_p1), .A1(4'b1010), .Y(compare_4_6_y));
  TC_ADDER_4 tc_adder_4_4 (
    .A(binary_to_bcd_converter_4_p1), .B(4'b0001), .O(tc_adder_4_4_o));  // open: Cin, Cout, Overflow
  COMPARE_4 compare_4_7 (.A0(binary_to_bcd_converter_4_p1), .A1(4'b1001), .Y(compare_4_7_y));
endmodule
